# Fritzing sketch fritzing (saved by Fritzing 1.0.6)
breadboards: 1

parts:
  Componente1 = Arduino Uno (Rev3)
  S2 = Momentary Switch [package=ksa_sealed_tac_switch]
  R1 = Resistor [tolerance=±5% power=0.25W resistance=220 package=THT]
  LED1 = LED - 5mm [color="Red (633nm)" current=0.030A package="5 mm [THT]"]
  LED2 = LED - 5mm [color="Red (633nm)" current=0.030A package="5 mm [THT]"]
  LED3 = LED - 5mm [color="Red (633nm)" current=0.030A package="5 mm [THT]"]
  LED4 = LED - 5mm [color="Red (633nm)" current=0.030A package="5 mm [THT]"]

nets:
  N1: Componente1.D8, LED4.anode
  N2: Componente1.D9_PWM, LED3.anode
  N3: Componente1.D10_PWM/SS, LED1.anode
  N4: Componente1.D11_PWM/MOSI, LED2.anode
  N5: Componente1.GND, R1.Pin_0, LED1.cathode, LED2.cathode, LED3.cathode, LED4.cathode
  N6: Componente1.D7, S2.3, R1.Pin_1
  N7: Componente1.5V, S2.1
